// Logisim project ALU-Team60.circ as structural Verilog: 1 circuit, main circuit main
module main (
  input  [15:0] A,
  input  [15:0] B,
  input  [2:0] C2C1C0,
  output [15:0] ALUOP,
  output out_5,
  output E
);

  wire adder_1_cout, adder_2_cout, subtractor_1_bout;
  wire [15:0] adder_1_out, adder_2_out, and_1_out, or_1_out, subtractor_1_out, xor_1_out;

  assign or_1_out = A | B;  // OR_Gate or_1, 16 bits wide
  assign and_1_out = A & B;  // AND_Gate and_1, 16 bits wide
  assign xor_1_out = A ^ B;  // XOR_Gate xor_1, 16 bits wide
  Adder #(.width(16)) adder_1 (.a(A), .b(16'h1), .out(adder_1_out), .cin(1'b0), .cout(adder_1_cout));
  Adder #(.width(16)) adder_2 (.a(A), .b(B), .out(adder_2_out), .cin(1'b0), .cout(adder_2_cout));
  Subtractor #(.width(16)) subtractor_1 (.a(A), .b(B), .out(subtractor_1_out), .bin(1'b0), .bout(subtractor_1_bout));
  or or_2 (E, adder_2_cout, subtractor_1_bout, adder_1_cout);
  Multiplexer #(.select(3), .width(16)) multiplexer_1 (
    .in1(adder_2_out), .in2(subtractor_1_out), .in3(A), .in4(and_1_out), .in5(or_1_out), .in6(xor_1_out),
    .in7(adder_1_out), .out(ALUOP), .sel(C2C1C0));  // open: in0, en
endmodule
