// Logisim project BUS-Team60.circ as structural Verilog: 1 circuit, main circuit main
module main (
  input  in_1,
  input  in_2,
  input  in_3,
  input  in_4,
  input  [2:0] in_5,
  input  in_6,
  input  [2:0] in_7,
  input  in_8,
  output out_9
);

  wire AC_prime, ACLOADING, and_1_out, and_4_out, and_5_out, and_6_out, and_7_out, and_8_out, and_9_out,
       and_10_out, and_11_out, ARLOAD, B0, B1, B2, B3, B4, B5, B6, B7, B8, B9, B10, B11, clock_1_out, D0,
       D0T4_2_out, D0T4_out, D0T5_out, D1, D1T4_2_out, D1T4_out, D2, D2T4_out, D2T5_out, D3, D4, D5,
       D5T4_2_out, D5T4_out, D5T5_2_out, D5T5_out, D6, D7, DRLOAD, I, IRLOAD, MEMOMRYWRITEENBALE,
       MEMORYREADINGENABLE, not_1_out, not_3_out, PCINC, PCLOAD, r, rB5_2_out, rB5_out, SCCLEAR, SCINC, T0,
       T2, T3, T4, T4D2_out, T5, T5D1_out, T6, T6D5_out, T7, T8, T9, T10, T11, T12, T13, T14, T15, undriven,
       undriven_2;
  wire [2:0] IR_q;
  wire [3:0] SC_q;
  wire [6:0] AR_q, bit_extender_1_out, bit_extender_3_out, PC_q;
  wire [15:0] AC_q, bit_extender_2_out, bit_extender_4_out, DR_q, main_1_aluop, multiplexer_1_out,
       ram_1_data, TR_q;

  Clock clock_1 (.out(clock_1_out));
  Bit_Extender #(.in_width(16), .out_width(7)) bit_extender_1 (.in(multiplexer_1_out), .out(bit_extender_1_out));
  ALU_Team60_main main_1 (.A(DR_q), .B(AC_q), .C2C1C0(in_7), .ALUOP(main_1_aluop), .E(out_9));  // open: out_5
  Register #(.width(7)) AR (.D(bit_extender_1_out), .en(in_3), .Q(AR_q), .clk(clock_1_out));  // open: clr
  Register #(.width(16)) TR (.D(multiplexer_1_out), .en(in_4), .Q(TR_q), .clk(clock_1_out));  // open: clr
  Register #(.width(16)) DR (.D(multiplexer_1_out), .en(in_6), .Q(DR_q), .clk(clock_1_out));  // open: clr
  Register #(.width(16)) AC (.D(main_1_aluop), .en(in_8), .Q(AC_q), .clk(clock_1_out));  // open: clr
  RAM #(.addrWidth(7), .dataWidth(16), .bus("separate")) ram_1 (
    .addr(AR_q), .din(multiplexer_1_out), .data(ram_1_data), .str(in_2), .clk(clock_1_out), .ld(in_1));  // open: sel, clr
  assign bit_extender_2_out = {{9{1'b0}}, AR_q};  // Bit_Extender bit_extender_2
  Bit_Extender #(.in_width(16), .out_width(7)) bit_extender_3 (.in(multiplexer_1_out), .out(bit_extender_3_out));
  Counter #(.width(7), .max('h7f)) PC (
    .D(bit_extender_3_out), .count(undriven), .Q(PC_q), .clk(clock_1_out));  // open: load, carry, clr
  assign bit_extender_4_out = {{9{1'b0}}, PC_q};  // Bit_Extender bit_extender_4
  Register #(.width(16)) IR (
    .D(multiplexer_1_out), .en(undriven_2), .Q({I, IR_q, B11, B10, B9, B8, B7, B6, B5, B4, B3, B2, B1, B0}),
    .clk(clock_1_out));  // open: clr
  Multiplexer #(.select(3), .width(16)) multiplexer_1 (
    .in0(ram_1_data), .in1(bit_extender_2_out), .in2(TR_q), .in3(DR_q), .in4(AC_q), .in5(bit_extender_4_out),
    .in6({I, IR_q, B11, B10, B9, B8, B7, B6, B5, B4, B3, B2, B1, B0}), .out(multiplexer_1_out), .sel(in_5));  // open: in7, en
  Counter #(.width(4), .max('hf)) SC (.Q(SC_q));  // open: load, D, count, carry, clk, clr
  not not_1 (not_1_out, I);
  and T3I_prime_D7 (r, T3, not_1_out, D7);
  Decoder #(.select(4)) decoder_1 (
    .out0(T0), .out1(IRLOAD), .out2(T2), .out3(T3), .out4(T4), .out5(T5), .out6(T6), .out7(T7), .out8(T8),
    .out9(T9), .out10(T10), .out11(T11), .out12(T12), .out13(T13), .out14(T14), .out15(T15), .en(SC_q[0]));  // open: sel
  Decoder #(.select(3)) decoder_2 (
    .out0(D0), .out1(D1), .out2(D2), .out3(D3), .out4(D4), .out5(D5), .out6(D6), .out7(D7), .en(IR_q[0]));  // open: sel
  or or_1 (PCINC, and_1_out, IRLOAD);
  and and_1 (and_1_out, r, AC_prime, B2);
  and and_2 (PCLOAD, T4, D4);
  or or_2 (ARLOAD, T0, T2);
  or D0T4_D1T4_D2T4_rB5_D5T5_D5T4 (DRLOAD, D0T4_out, D1T4_out, D2T4_out, rB5_out, D5T5_out, D5T4_out);
  and and_3 (MEMOMRYWRITEENBALE, T4, D3);
  and D0T4 (D0T4_out, D0, T4);
  and D1T4 (D1T4_out, D1, T4);
  and D2T4 (D2T4_out, D2, T4);
  and rB5 (rB5_out, r, B5);
  and D5T5 (D5T5_out, D5, T5);
  and D5T4 (D5T4_out, D5, T4);
  or or_3 (MEMORYREADINGENABLE, T4D2_out, D1T4_2_out, D5T4_2_out, D0T4_2_out, IRLOAD);
  or or_4 (ACLOADING, D2T5_out, T5D1_out, D5T5_2_out, T6D5_out, rB5_2_out, D0T5_out);
  and T4D2 (T4D2_out, T4, D2);
  and D1T4_2 (D1T4_2_out, T4, D1);
  and D5T4_2 (D5T4_2_out, T4, D5);
  and D0T4_2 (D0T4_2_out, T4, D0);
  and D2T5 (D2T5_out, D2, T5);
  and T5D1 (T5D1_out, D1, T5);
  and D5T5_2 (D5T5_2_out, D5, T5);
  and T6D5 (T6D5_out, D5, T6);
  and rB5_2 (rB5_2_out, r, B5);
  and D0T5 (D0T5_out, D0, T5);
  not not_2 (SCINC, SCCLEAR);
  or or_5 (SCCLEAR, and_4_out, and_5_out, and_6_out, and_7_out, and_8_out, and_9_out, and_10_out, and_11_out);
  and and_4 (and_4_out, T5, D2);
  and and_5 (and_5_out, T5, D1);
  and and_6 (and_6_out, T6, D5);
  and and_7 (and_7_out, r, AC_prime, B2);
  and and_8 (and_8_out, T4, D4);
  and and_9 (and_9_out, T5, D0);
  and and_10 (and_10_out, T4, D3);
  and and_11 (and_11_out, T4, not_3_out, D7, B5);
  not not_3 (not_3_out, I);
  // Pins of 1 and 3 bits meet at IR_q
  // Pins of 1 and 4 bits meet at SC_q

  // Other names for the same wires on the sheet: T1 = IRLOAD
endmodule
